# Fritzing sketch Mobile_sensor (saved by Fritzing 0.9.4)
breadboards: 1

parts:
  R1 = Resistor [tolerance=±5% resistance=100 package="2512 [SMD]"]
  R2 = Resistor [tolerance=±5% resistance=100 package="2512 [SMD]"]
  Argon1 = Particle Argon
  LED2 = LED - 3mm [color="Green (560nm)" package="3 mm [THT]"]
  LED3 = LED - 3mm [color="Red (633nm)" package="3 mm [THT]"]
  S1 = Toggle Switch [package=THT]
  Part1 = Adafruit MicroSD card breakout board [part_number="Adafruit #254"]
  Part2 = MQ-131 breakout

nets:
  N1: R1.Pin_0, LED2.cathode
  GND: R1.Pin_1, R2.Pin_1, S1.L2, Part1.GND, Part2.GND
  N2: R2.Pin_0, LED3.cathode
  N3: Argon1.A1, LED3.anode
  N4: Argon1.A2, Part2.AO
  N5: Argon1.A3, LED2.anode
  N6: Argon1.A4, S1.COM
  N7: Argon1.A5, Part1.CS
  N8: Argon1.SCK, Part1.CLK
  N9: Argon1.MO, Part1.DI
  N10: Argon1.MI, Part1.DO
  +3V3: S1.L1, Part1.+3V3, Part2.VCC

notes:
  3.7 Li-po

custom parts:
  Particle Argon: The Argon is a powerful Wi-Fi enabled development board that can act as either a standalone Wi-Fi endpoint or Wi-Fi enabled gateway for Particle Mesh networks. It is based on the Nordic nRF52840 and has built-in battery charging circuitry so it’s easy to connect a Li-Po and deploy your local network in minutes. The Argon is great for connecting existing projects to the Particle Device Cloud or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
  Adafruit MicroSD card breakout board: Not just a simple breakout board, this microSD adapter goes the extra mile - designed for ease of use. Onboard 5v->3v regulator provides 150mA for power-hungry cards 3v level shifting means you can use this with ease on either 3v or 5v systems Uses a proper level shifting chip, not resistors: less problems, and faster read/write access Use 3 or 4 digital pins to read and write 2Gb+ of storage!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
  MQ-131 breakout: SKU: 101282
